# Fritzing sketch AICameraTrafficLights (saved by Fritzing 0.9.3b)
breadboards: 1

parts:
  A1 = Arduino UNO R4 WiFi
  R1 = Resistor [tolerance=±5% resistance=220 package=THT]
  LED1 = LED - 5mm [color="Red (633nm)" package="5 mm [THT]"]
  LED2 = LED - 5mm [color="Orange (605nm)" package="5 mm [THT]"]
  LED3 = LED - 5mm [color="Green (555nm)" package="5 mm [THT]"]
  R2 = Resistor [tolerance=±5% resistance=220 package=THT]
  R3 = Resistor [tolerance=±5% resistance=220 package=THT]
  R4 = Resistor [tolerance=±5% resistance=220 package=THT]
  R5 = Resistor [tolerance=±5% resistance=220 package=THT]
  R6 = Resistor [tolerance=±5% resistance=220 package=THT]
  LED4 = LED - 5mm [color="Red (633nm)" package="5 mm [THT]"]
  LED5 = LED - 5mm [color="Green (555nm)" package="5 mm [THT]"]
  LED6 = LED - 5mm [color="Orange (605nm)" package="5 mm [THT]"]
  HuskyLens = HuskyLens-Vision-Sensor_1
  Servo = Basic Servo
  12V = Power plug
  C1 = Electrolytic Capacitor [capacitance=100µF voltage=16V package="100 mil [THT, electrolytic]"]

nets:
  N1: A1.Pin_8, A1.Pin_27, HuskyLens.pin4
  N2: A1.Pin_9, A1.Pin_10, A1.Pin_18, A1.Pin_48, R1.Pin_0, R2.Pin_0, R3.Pin_0, R4.Pin_0, R5.Pin_0, R6.Pin_0, HuskyLens.pin3
  N3: A1.Pin_37, Servo.pulse
  VCC: A1.Pin_39, Servo.vcc, 12V.VCC, C1.+
  N4: A1.Pin_41, LED3.anode
  N5: A1.Pin_42, LED2.anode
  N6: A1.Pin_43, LED1.anode
  N7: A1.Pin_44, LED5.anode
  N8: A1.Pin_45, LED6.anode
  N9: A1.Pin_46, LED4.anode
  N10: A1.Pin_50, HuskyLens.pin1
  N11: A1.Pin_51, HuskyLens.pin2
  N12: R1.Pin_1, LED1.cathode
  N13: LED2.cathode, R3.Pin_1
  N14: LED3.cathode, R2.Pin_1
  N15: R4.Pin_1, LED5.cathode
  N16: R5.Pin_1, LED4.cathode
  N17: R6.Pin_1, LED6.cathode
  GND: Servo.gnd, 12V.GND, C1.-

custom parts:
  Arduino UNO R4 WiFi: The Arduino UNO R4 WiFi merges the RA4M1 microprocessor from Renesas with the ESP32-S3 from Espressif, creating an all-in-one tool for makers with enhanced processing power and a diverse array of new peripherals.
  HuskyLens-Vision-Sensor_1: Huskylens is an easy-to-use AI Camera | Vision Sensor. DFrobot Huskylens is equipped with multiple functions, such as face recognition, object tracking, object recognition, line tracking, color recognition, and tag(QR code) recognition.
